// Logisim project Lab4.circ as structural Verilog: 1 circuit, main circuit main
module main (
  input  A,
  input  B,
  input  C,
  input  D
);

  wire and_1_out, and_2_out, and_3_out, and_4_out, or_1_out;

  and and_1 (and_1_out, ~A, B, ~C, D);  // AND_Gate
  and and_2 (and_2_out, A, ~B, C, ~D);  // AND_Gate
  and and_3 (and_3_out, A, B, C, D);
  and and_4 (and_4_out, ~A, ~B, ~C, ~D);  // AND_Gate
  or or_1 (or_1_out, and_1_out, and_2_out, and_3_out, and_4_out);
  // Probe on or_1_out

  // Notes on the sheet:
  //   F
endmodule
